# Fritzing sketch UPDATED CSL AQI long board.2 (saved by Fritzing 0.9.9b)
breadboards: 1

parts:
  Part1 = Adafruit Feather M0 WINC1500 [part_number="Adafruit #3010"]
  Part3 = Adafruit BME280 [part_number="Adafruit #2652"]
  Part4 = Adafruit TPS61023 [part_number="Adafruit #4654"]
  J1 = SPS30 PM sensirion [package=THT]
  Part6 = Adafruit SCD30 [part_number="Adafruit #4867"]
  Part7 = Adafruit 128x64 OLED FeatherWing [part_number="Adafruit #4650"]
  Part8 = Adafruit Adalogger FeatherWing [part_number="Adafruit #2922"]

nets:
  N1: Part1.WAKE, Part7.16, Part8.G
  N2: Part1.D1, J1.RX/SDA, Part7.15, Part8.TX
  N3: Part1.D0, J1.TX/SCL, Part7.14, Part8.RX
  N4: Part1.MISO, Part7.13, Part8.MISO
  N5: Part1.MOSI, Part7.12, Part8.MOSI
  N6: Part1.SCK, Part7.11, Part8.SCK
  N7: Part1.A5, Part7.10, Part8.F
  N8: Part1.A4, Part7.9, Part8.E
  N9: Part1.A3, Part7.8, Part8.D
  N10: Part1.A2, Part7.7, Part8.C
  N11: Part1.A1, Part7.6, Part8.B
  N12: Part1.A0, Part7.5, Part8.A
  GND: Part1.GND, Part3.GND, Part4.GND, J1.GND, Part6.GND, Part7.GND, Part8.GND
  N13: Part1.AREF, Part7.3, Part8.AREF
  +3V3: Part1.+3V3, Part3.VCC, Part4.VIN, Part6.VCC, Part7.3.3V, Part8.+3V3
  N14: Part1.!RESET, Part7.!RESET, Part8.RESET
  N15: Part1.VBAT, Part7.28, Part8.VBAT
  N16: Part1.EN, Part7.27, Part8.EN
  N17: Part1.VBUS, Part7.26, Part8.USB
  N18: Part1.D13, Part7.25, Part8.N
  N19: Part1.D12, Part7.24, Part8.M
  N20: Part1.D11, Part7.23, Part8.L
  N21: Part1.D10, Part7.22, Part8.CS
  N22: Part1.D9, Part7.J, Part8.J
  N23: Part1.D6, Part7.I, Part8.I
  N24: Part1.D5, Part7.H, Part8.H
  N25: Part1.SCL, Part3.SCK/SCL, Part6.SCL, Part7.SCL, Part8.SCL
  N26: Part1.SDA, Part3.SDO/ADR, Part6.SDA, Part7.SDA, Part8.SDA
  VDD: Part4.VDD, J1.VDD

custom parts:
  Adafruit Feather M0 WINC1500: This is the Adafruit Feather M0 WiFi w/ATWINC1500 - our take on an 'all-in-one' Arduino-compatible + high speed, reliable WiFi with built in USB and battery charging. Its an Adafruit Feather M0 with a WiFi module, ready to rock! Connect your Feather to the Internet with this fine new FCC-certified WiFi module from Atmel. This 802.11bgn-capable WiFi module is the best new thing for networking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
  Adafruit BME280: Bosch has stepped up their game with their new BME280 sensor, an environmental sensor with temperature, barometric pressure and humidity! This sensor is great for all sorts of indoor environmental sensing and can even be used in both I2C and SPI! This precision sensor from Bosch is the best low-cost sensing solution for measuring humidity with ±3% accuracy, barometric pressure with ±1 hPa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
  Adafruit TPS61023: This adorable little board will come in very handy whenever you need a good amount of 5V power. It's the size of a linear regulator, but it's actually a mini-booster! Input 2-5VDC on one side, and get 5V at up to 1A supply on the other. Perfect for use with battery-powered projects with 2 or 3 Alkaline, or a single Lithium battery. This booster uses a very small but thermally efficient chip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
  Adafruit 128x64 OLED FeatherWing: A Feather board without ambition is a Feather board without FeatherWings! This is the FeatherWing 128x64 OLED: it adds a gorgeous 128x64 monochrome OLED plus 3 user buttons to any Feather main board. Using our Feather Stacking Headers or Feather Female Headers you can connect a FeatherWing on top of your Feather board and let the board take flight! These displays are small, only about 1.3"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
  Adafruit Adalogger FeatherWing: This is the Adalogger FeatherWing: it adds both a battery-backed Real Time Clock and micro SD card storage to any Feather main board. This FeatherWing will make it real easy to add datalogging to any of our existing Feathers. You get both an I2C real time clock (PCF8523) with 32KHz crystal and battery backup, and a microSD socket that connects to the SPI port pins (+ extra pin for CS). Tested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
